// Logisim project ArrayFilter.circ as structural Verilog: 6 circuits, main circuit main
module main (
  input  [7:0] data,
  input  data_av,
  output [2:0] Current_State,
  output done
);

  wire arrayfilter_1_ld, arrayfilter_1_sel, button_1_out, clock_1_out, not_1_out;
  wire [7:0] arrayfilter_1_address, arrayfilter_1_data_out, controlled_buffer_1_out;

  // Probe on data
  Clock clock_1 (.out(clock_1_out));
  // Probe on Current_State
  Button button_1 (.out(button_1_out));
  ArrayFilter arrayfilter_1 (
    .data(data), .data_in(controlled_buffer_1_out), .Current_State(Current_State), .data_av(data_av),
    .clk(clock_1_out), .rst(button_1_out), .address(arrayfilter_1_address),
    .data_out(arrayfilter_1_data_out), .sel(arrayfilter_1_sel), .ld(arrayfilter_1_ld), .done(done));
  not not_1 (not_1_out, arrayfilter_1_ld);
  assign controlled_buffer_1_out = arrayfilter_1_ld ? arrayfilter_1_data_out : 8'bz;  // Controlled_Buffer controlled_buffer_1
  RAM ram_1 (
    .addr(arrayfilter_1_address), .data(controlled_buffer_1_out), .sel(arrayfilter_1_sel), .clk(clock_1_out),
    .ld(not_1_out));  // open: clr
endmodule

module ArrayFilter (
  input  [7:0] data,
  input  [7:0] data_in,
  input  data_av,
  input  clk,
  input  rst,
  output [7:0] address,
  output [7:0] data_out,
  output sel,
  output ld,
  output done,
  output [2:0] Current_State
);

  wire controlpath_1_selmuxadder0, controlpath_1_selmuxadder1, controlpath_1_selmuxaddress,
       controlpath_1_selmuxcomp0, controlpath_1_selmuxcomp1, controlpath_1_selmuxreg, controlpath_1_wraux,
       controlpath_1_wri, controlpath_1_wrj, controlpath_1_wrsize, datapath_1_comp;

  ControlPath controlpath_1 (
    .data_av(data_av), .comp(datapath_1_comp), .clk(clk), .rst(rst), .Current_State(Current_State),
    .wrI(controlpath_1_wri), .wrJ(controlpath_1_wrj), .wrSize(controlpath_1_wrsize),
    .selMuxAdder1(controlpath_1_selmuxadder1), .wrAux(controlpath_1_wraux),
    .selMuxReg(controlpath_1_selmuxreg), .selMuxAdder0(controlpath_1_selmuxadder0),
    .selMuxAddress(controlpath_1_selmuxaddress), .selMuxComp1(controlpath_1_selmuxcomp1),
    .selMuxComp0(controlpath_1_selmuxcomp0), .sel(sel), .ld(ld), .done(done));
  DataPath datapath_1 (
    .data(data), .rst(rst), .clk(clk), .data_in(data_in), .selMuxReg(controlpath_1_selmuxreg),
    .wrI(controlpath_1_wri), .wrSize(controlpath_1_wrsize), .wrJ(controlpath_1_wrj),
    .wrAux(controlpath_1_wraux), .selMuxAdder0(controlpath_1_selmuxadder0),
    .selMuxAdder1(controlpath_1_selmuxadder1), .selMuxAddress(controlpath_1_selmuxaddress),
    .selMuxComp0(controlpath_1_selmuxcomp0), .selMuxComp1(controlpath_1_selmuxcomp1), .address(address),
    .comp(datapath_1_comp), .data_out(data_out));
endmodule

module DataPath (
  input  wrJ,
  input  selMuxAddress,
  input  selMuxAdder0,
  input  selMuxAdder1,
  input  [7:0] data,
  input  selMuxReg,
  input  wrI,
  input  selMuxComp0,
  input  wrSize,
  input  selMuxComp1,
  input  rst,
  input  clk,
  input  [7:0] data_in,
  input  wrAux,
  output [7:0] address,
  output comp,
  output [7:0] data_out
);

  wire [7:0] adder_1_out, multiplexer_1_out, multiplexer_2_out, multiplexer_3_out, multiplexer_5_out,
       multiplexer_6_out, reg_I_q, reg_J_q, reg_size_q;

  // Probe on data
  Multiplexer #(.width(8), .enable("false")) multiplexer_1 (
    .in0(adder_1_out), .in1(data), .out(multiplexer_1_out), .sel(selMuxReg));
  Register reg_J (.D(multiplexer_1_out), .en(wrJ), .Q(reg_J_q), .clk(clk), .clr(rst));
  Register reg_I (.D(multiplexer_1_out), .en(wrI), .Q(reg_I_q), .clk(clk), .clr(rst));
  Register reg_size (.D(adder_1_out), .en(wrSize), .Q(reg_size_q), .clk(clk), .clr(rst));
  Multiplexer #(.width(8), .enable("false")) multiplexer_2 (
    .in0(reg_J_q), .in1(reg_I_q), .out(multiplexer_2_out), .sel(selMuxAdder0));
  Multiplexer #(.width(8), .enable("false")) multiplexer_3 (
    .in0(8'h1), .in1(multiplexer_1_out), .out(multiplexer_3_out), .sel(selMuxAdder1));
  Register reg_Aux (.D(data_in), .en(wrAux), .Q(data_out), .clk(clk), .clr(rst));
  Adder adder_1 (.a(multiplexer_2_out), .b(multiplexer_3_out), .out(adder_1_out));  // open: cin, cout
  Multiplexer #(.width(8), .enable("false")) multiplexer_4 (
    .in0(reg_J_q), .in1(reg_I_q), .out(address), .sel(selMuxAddress));
  Multiplexer #(.width(8), .enable("false")) multiplexer_5 (
    .in0({8{1'b0}}), .in1(reg_I_q), .out(multiplexer_5_out), .sel(selMuxComp0));
  Multiplexer #(.width(8), .enable("false")) multiplexer_6 (
    .in0(reg_size_q), .in1(data_out), .out(multiplexer_6_out), .sel(selMuxComp1));
  Comparator comparator_1 (.a(multiplexer_5_out), .b(multiplexer_6_out), .lt(comp));  // open: gt, eq
endmodule

module ControlPath (
  input  data_av,
  input  comp,
  input  clk,
  input  rst,
  output wrI,
  output wrJ,
  output wrSize,
  output selMuxAdder1,
  output wrAux,
  output [2:0] Current_State,
  output selMuxReg,
  output selMuxAdder0,
  output selMuxAddress,
  output selMuxComp1,
  output selMuxComp0,
  output sel,
  output ld,
  output done
);

  wire [2:0] nextstate_1_d0;

  NextState nextstate_1 (
    .Q2(Current_State[2]), .Q1(Current_State[1]), .Q0(Current_State[0]), .data_av(data_av), .comp(comp),
    .D2(nextstate_1_d0[2]), .D1(nextstate_1_d0[1]), .D0(nextstate_1_d0[0]));
  Register #(.width(3)) register_1 (.D(nextstate_1_d0), .Q(Current_State), .clk(clk), .clr(rst));  // open: en
  Output output_1 (
    .D2(Current_State[2]), .D1(Current_State[1]), .D0(Current_State[0]), .wrI(wrI), .wrJ(wrJ),
    .wrSize(wrSize), .selMuxAdder1(selMuxAdder1), .wrAux(wrAux), .selMuxReg(selMuxReg),
    .selMuxAdder0(selMuxAdder0), .selMuxAddress(selMuxAddress), .selMuxComp0(selMuxComp0),
    .selMuxComp1(selMuxComp1), .sel(sel), .ld(ld), .done(done));
endmodule

module NextState (
  input  Q2,
  input  Q1,
  input  Q0,
  input  data_av,
  input  comp,
  output D2,
  output D1,
  output D0
);

  wire and_1_out, and_2_out, and_3_out, and_4_out, and_5_out, and_6_out, and_7_out, and_8_out, and_9_out,
       and_10_out, and_11_out, and_12_out, not_1_out, not_2_out, not_3_out, not_4_out, not_5_out, not_6_out,
       not_7_out, not_8_out, not_9_out, not_10_out, not_11_out, not_12_out, not_13_out, not_14_out,
       not_15_out, not_16_out, not_17_out;

  not not_1 (not_1_out, Q2);
  not not_2 (not_2_out, Q1);
  not not_3 (not_3_out, Q1);
  not not_4 (not_4_out, Q1);
  not not_5 (not_5_out, Q2);
  not not_6 (not_6_out, comp);
  not not_7 (not_7_out, Q0);
  not not_8 (not_8_out, Q1);
  not not_9 (not_9_out, comp);
  not not_10 (not_10_out, Q1);
  not not_11 (not_11_out, Q0);
  not not_12 (not_12_out, Q2);
  not not_13 (not_13_out, Q1);
  not not_14 (not_14_out, data_av);
  not not_15 (not_15_out, Q2);
  not not_16 (not_16_out, comp);
  not not_17 (not_17_out, Q0);
  and and_1 (and_1_out, not_1_out, Q1, Q0);
  and and_2 (and_2_out, Q2, not_2_out, comp);
  and and_3 (and_3_out, Q2, not_3_out, Q0);
  and and_4 (and_4_out, not_4_out, Q0, data_av);
  and and_5 (and_5_out, not_5_out, Q1, not_6_out);
  and and_6 (and_6_out, Q1, not_7_out);
  and and_7 (and_7_out, Q2, not_8_out, not_9_out);
  and and_8 (and_8_out, Q2, not_10_out, Q0);
  and and_9 (and_9_out, not_11_out, data_av);
  and and_10 (and_10_out, not_12_out, not_13_out, Q0, not_14_out);
  and and_11 (and_11_out, not_15_out, Q1, Q0, not_16_out);
  and and_12 (and_12_out, Q2, not_17_out);
  or or_1 (D2, and_1_out, and_2_out, and_3_out);
  or or_2 (D1, and_4_out, and_5_out, and_6_out, and_7_out, and_8_out);
  or or_3 (D0, and_9_out, and_10_out, and_11_out, and_12_out);
endmodule

module Output (
  input  D2,
  input  D1,
  input  D0,
  output wrI,
  output wrJ,
  output wrSize,
  output selMuxAdder1,
  output wrAux,
  output selMuxReg,
  output selMuxAdder0,
  output selMuxAddress,
  output selMuxComp0,
  output selMuxComp1,
  output sel,
  output ld,
  output done
);

  wire and_6_out, and_7_out, and_8_out, and_9_out, and_13_out, and_14_out, not_1_out, not_2_out, not_3_out,
       not_4_out, not_5_out, not_6_out, not_7_out, not_8_out, not_9_out, not_10_out, not_11_out, not_12_out,
       not_13_out, not_14_out, not_15_out, not_16_out, not_17_out, not_18_out, not_19_out, not_20_out,
       not_21_out;

  not not_1 (not_1_out, D1);
  not not_2 (not_2_out, D0);
  not not_3 (not_3_out, D0);
  not not_4 (not_4_out, D2);
  not not_5 (not_5_out, D1);
  not not_6 (not_6_out, D2);
  not not_7 (not_7_out, D2);
  not not_8 (not_8_out, D1);
  not not_9 (not_9_out, D2);
  not not_10 (not_10_out, D0);
  not not_11 (not_11_out, D2);
  not not_12 (not_12_out, D1);
  not not_13 (not_13_out, D1);
  not not_14 (not_14_out, D0);
  not not_15 (not_15_out, D2);
  not not_16 (not_16_out, D2);
  not not_17 (not_17_out, D1);
  not not_18 (not_18_out, D0);
  not not_19 (not_19_out, D2);
  not not_20 (not_20_out, D1);
  not not_21 (not_21_out, D1);
  and and_1 (done, D2, D1, D0);
  and and_2 (wrI, not_1_out, not_2_out);
  and and_3 (wrJ, D1, not_3_out);
  and and_4 (selMuxAdder1, not_4_out, not_5_out, D0);
  and and_5 (wrAux, not_6_out, D1, D0);
  and and_6 (and_6_out, not_7_out, not_8_out);
  and and_7 (and_7_out, not_9_out, not_10_out);
  and and_8 (and_8_out, not_11_out, not_12_out, D0);
  and and_9 (and_9_out, D2, not_13_out, not_14_out);
  and and_10 (selMuxAddress, not_15_out, D1, D0);
  and and_11 (selMuxComp0, not_16_out, D1, D0);
  and and_12 (selMuxComp1, D2, not_17_out, not_18_out);
  and and_13 (and_13_out, not_19_out, D1, D0);
  and and_14 (and_14_out, D2, not_20_out, D0);
  and and_15 (ld, D2, not_21_out, D0);
  or or_1 (selMuxReg, and_6_out, and_7_out);
  or or_2 (selMuxAdder0, and_8_out, and_9_out);
  or or_3 (sel, and_13_out, and_14_out);

  assign wrSize = selMuxAdder1;
endmodule
